// Logisim project 12-bit-risc-v-microprocessor.circ as structural Verilog: 4 circuits, main circuit main
module main (
);

  register_file_12_bit register_file_12_bit_1 ();  // open: Write_Enabler, Write_Data, RD_Selector, DATA_1_RS, RS_Selector, DATA_2_RT, RT_Selector, CLOCK, Register_Clear
  ALU_12_bit alu_12_bit_1 ();  // open: A, B, Zero_Detector, Result, ALUOP, Cout___Bout___Upper_Bits_of_Product___Remainder
endmodule

module register_file_12_bit (
  input  Write_Enabler,
  input  [11:0] Write_Data,
  input  [2:0] RS_Selector,
  input  [2:0] RD_Selector,
  input  [2:0] RT_Selector,
  input  CLOCK,
  input  Register_Clear,
  output [11:0] DATA_1_RS,
  output [11:0] DATA_2_RT
);

  wire and_1_out, and_2_out, and_3_out, and_4_out, and_5_out, and_6_out, and_7_out, and_8_out,
       decoder_1_out0, decoder_1_out1, decoder_1_out2, decoder_1_out3, decoder_1_out4, decoder_1_out5,
       decoder_1_out6, decoder_1_out7;
  wire [11:0] R0_q, R1_q, R2_q, R3_q, R4_q, R5_q, R6_q, R7_q;

  Decoder #(.select(3), .enable("false")) decoder_1 (
    .out0(decoder_1_out0), .out1(decoder_1_out1), .out2(decoder_1_out2), .out3(decoder_1_out3),
    .out4(decoder_1_out4), .out5(decoder_1_out5), .out6(decoder_1_out6), .out7(decoder_1_out7),
    .sel(RD_Selector));
  and and_1 (and_1_out, Write_Enabler, decoder_1_out0);
  and and_2 (and_2_out, Write_Enabler, decoder_1_out1);
  and and_3 (and_3_out, Write_Enabler, decoder_1_out2);
  and and_4 (and_4_out, Write_Enabler, decoder_1_out3);
  Register #(.width(12)) R0 (.D(Write_Data), .en(and_1_out), .Q(R0_q), .clk(CLOCK), .clr(Register_Clear));
  Register #(.width(12)) R1 (.D(Write_Data), .en(and_2_out), .Q(R1_q), .clk(CLOCK), .clr(Register_Clear));
  Register #(.width(12)) R2 (.D(Write_Data), .en(and_3_out), .Q(R2_q), .clk(CLOCK), .clr(Register_Clear));
  Register #(.width(12)) R3 (.D(Write_Data), .en(and_4_out), .Q(R3_q), .clk(CLOCK), .clr(Register_Clear));
  Register #(.width(12)) R7 (.D(Write_Data), .en(and_5_out), .Q(R7_q), .clk(CLOCK), .clr(Register_Clear));
  Register #(.width(12)) R6 (.D(Write_Data), .en(and_6_out), .Q(R6_q), .clk(CLOCK), .clr(Register_Clear));
  Register #(.width(12)) R5 (.D(Write_Data), .en(and_7_out), .Q(R5_q), .clk(CLOCK), .clr(Register_Clear));
  Register #(.width(12)) R4 (.D(Write_Data), .en(and_8_out), .Q(R4_q), .clk(CLOCK), .clr(Register_Clear));
  and and_5 (and_5_out, Write_Enabler, decoder_1_out7);
  and and_6 (and_6_out, Write_Enabler, decoder_1_out6);
  and and_7 (and_7_out, Write_Enabler, decoder_1_out5);
  and and_8 (and_8_out, Write_Enabler, decoder_1_out4);
  Multiplexer #(.select(3), .width(12), .enable("false")) multiplexer_1 (
    .in0(R0_q), .in1(R1_q), .in2(R2_q), .in3(R3_q), .in4(R4_q), .in5(R5_q), .in6(R6_q), .in7(R7_q),
    .out(DATA_1_RS), .sel(RS_Selector));
  Multiplexer #(.select(3), .width(12), .enable("false")) multiplexer_2 (
    .in0(R0_q), .in1(R1_q), .in2(R2_q), .in3(R3_q), .in4(R4_q), .in5(R5_q), .in6(R6_q), .in7(R7_q),
    .out(DATA_2_RT), .sel(RT_Selector));
endmodule

module ALU_12_bit (
  input  [11:0] A,
  input  [11:0] B,
  input  [2:0] ALUOP,
  output Zero_Detector,
  output [11:0] Result,
  output [11:0] Cout___Bout___Upper_Bits_of_Product___Remainder
);

  wire adder_1_cout, subtractor_1_bout;
  wire [11:0] adder_1_out, and_1_out, bit_extender_1_out, bit_extender_2_out, divider_1_out, divider_1_rem,
       multiplier_1_cout, multiplier_1_out, not_1_out, or_1_out, subtractor_1_out, xor_1_out;

  assign not_1_out = ~A;  // NOT_Gate not_1, 12 bits wide
  Adder #(.width(12)) adder_1 (.a(A), .b(B), .out(adder_1_out), .cout(adder_1_cout));  // open: cin
  Subtractor #(.width(12)) subtractor_1 (.a(A), .b(B), .out(subtractor_1_out), .bout(subtractor_1_bout));  // open: bin
  Multiplier #(.width(12)) multiplier_1 (.a(A), .b(B), .out(multiplier_1_out), .cout(multiplier_1_cout));  // open: cin
  Divider #(.width(12)) divider_1 (.a(A), .b(B), .out(divider_1_out), .rem(divider_1_rem));  // open: upper
  assign and_1_out = A & B;  // AND_Gate and_1, 12 bits wide
  assign or_1_out = A | B;  // OR_Gate or_1, 12 bits wide
  assign xor_1_out = A ^ B;  // XOR_Gate xor_1, 12 bits wide
  Multiplexer #(.select(3), .width(12), .enable("false")) multiplexer_1 (
    .in0(and_1_out), .in1(or_1_out), .in2(not_1_out), .in3(xor_1_out), .in4(adder_1_out),
    .in5(subtractor_1_out), .in6(multiplier_1_out), .in7(divider_1_out), .out(Result), .sel(ALUOP));
  assign bit_extender_1_out = {{11{1'b0}}, adder_1_cout};  // Bit_Extender bit_extender_1
  assign bit_extender_2_out = {{11{1'b0}}, subtractor_1_bout};  // Bit_Extender bit_extender_2
  Multiplexer #(.select(3), .width(12), .enable("false")) multiplexer_2 (
    .in0({12{1'b0}}), .in1({12{1'b0}}), .in2({12{1'b0}}), .in3({12{1'b0}}), .in4(bit_extender_1_out),
    .in5(bit_extender_2_out), .in6(multiplier_1_cout), .in7(divider_1_rem),
    .out(Cout___Bout___Upper_Bits_of_Product___Remainder), .sel(ALUOP));
  nor nor_1 (Zero_Detector, Result[0], Result[1], Result[2], Result[3], Result[4], Result[5], Result[6], Result[7], Result[8], Result[9], Result[10], Result[11]);
endmodule

module Datapath (
  input  [2:0] ALUOP,
  input  Write_Enabler,
  output [2:0] Opcode,
  output [2:0] RS,
  output Zero,
  output [2:0] RT,
  output [2:0] RD,
  output [11:0] Data_1_RS,
  output [11:0] Result,
  output [11:0] Data_2_RT,
  output [11:0] Result_2
);

  wire clock_1_out, CLR_2_out, CLR_out;
  wire [11:0] adder_1_out, register_1_q;

  Register #(.width(12)) register_1 (.D(adder_1_out), .Q(register_1_q), .clk(clock_1_out), .clr(CLR_out));  // open: en
  Button CLR (.out(CLR_out));
  Clock clock_1 (.out(clock_1_out));
  Adder #(.width(12)) adder_1 (.a(register_1_q), .b(12'h1), .out(adder_1_out));  // open: cin, cout
  ROM #(.addrWidth(12), .dataWidth(12)) rom_1 (.addr(register_1_q), .data({Opcode, RS, RT, RD}));  // open: sel
  register_file_12_bit register_file_12_bit_1 (
    .Write_Enabler(Write_Enabler), .Write_Data(Result), .RD_Selector(RD), .DATA_1_RS(Data_1_RS),
    .RS_Selector(RS), .DATA_2_RT(Data_2_RT), .RT_Selector(RT), .CLOCK(clock_1_out), .Register_Clear(CLR_2_out));
  Button CLR_2 (.out(CLR_2_out));
  ALU_12_bit alu_12_bit_1 (
    .A(Data_1_RS), .B(Data_2_RT), .Zero_Detector(Zero), .Result(Result), .ALUOP(ALUOP),
    .Cout___Bout___Upper_Bits_of_Product___Remainder(Result_2));
endmodule
